# Fritzing sketch robot_project_circuit_drawing (saved by Fritzing 0.9.3b)
breadboards: 1

parts:
  IC1 = L293D [package=THT]
  Parça1 = Arduino Uno (Rev3)
  M1 = DC Motor
  M2 = DC Motor
  VCC1 = Battery block 9V
  hc-sr1 = hc-sr04
  hc-sr2 = hc-sr04
  hc-sr3 = hc-sr04

nets:
  N1: IC1.In_1, Parça1.D9_PWM
  N2: IC1.Out_1_(_Controlled_by_Enable_1_), M2.pin_2
  N3: IC1.0V, VCC1.-
  N4: IC1.Out_2_(_Controlled_by_Enable_1_), M2.pin_1
  N5: IC1.In_2, Parça1.D10_PWM/SS
  N6: IC1.+Vmotor, VCC1.+
  VCC: IC1.Enable_2, IC1.+V, hc-sr1.VCC, hc-sr2.VCC, hc-sr3.VCC
  N7: IC1.In_3, Parça1.D5_PWM
  N8: IC1.Out_3_(_Controlled_by_Enable_2_), M1.pin_2
  N9: IC1.Out_4_(_Controlled_by_Enable_2_), M1.pin_1
  N10: IC1.In_4, Parça1.D4
  N11: Parça1.A0, hc-sr3.Trig
  N12: Parça1.A1, hc-sr3.Echo
  N13: Parça1.A3, hc-sr2.Trig
  N14: Parça1.A4/SDA, hc-sr2.Echo
  N15: Parça1.D11_PWM/MOSI, hc-sr1.Echo
  N16: Parça1.D12/MISO, hc-sr1.Trig
  GND: hc-sr1.GND, hc-sr2.GND, hc-sr3.GND

notes:
  İdris İbrahim ERTEN
